# Fritzing sketch WasserSensor_Prototyp1 (saved by Fritzing 0.9.1b)
breadboards: 1

parts:
  Bauteil1 = Arduino Uno (Rev3)
  R1 = Resistor [tolerance=±5% resistance=220 package=THT]
  LED1 = LED - 5mm [color="Red (633nm)" package="5 mm [THT]"]
  J1 = female pin header, 2 pins [form="♀ (female)"]
  JP1 = FTDI_BASIC [package=ftdi_basic]

nets:
  N1: Bauteil1.A0, J1.pin2
  N2: Bauteil1.D10_PWM/SS, R1.Pin_1
  N3: Bauteil1.GND, LED1.cathode, J1.pin1, JP1.5
  N4: Bauteil1.D3_PWM, JP1.3
  N5: Bauteil1.D4, JP1.2
  N6: R1.Pin_0, LED1.anode

notes:
  Wasser-Sensor
  FTDI
  FTDI (Konsole via FTDI-USB-Kabel)
