# Fritzing sketch WasserSensor_Prototyp2 (saved by Fritzing 0.9.1b)
breadboards: 1

parts:
  IC1 = Voltage Regulator [part_number=7805 package=78xxl]
  C1 = Electrolytic Capacitor [capacitance=100µF package="200 mil [THT, electrolytic]"]
  U1 = attiny85 [package=dip]
  LED1 = smd LED [color="Red (633nm)" package="0603 [SMD]"]
  Q1 = npn-Powertransistor [part_number=TIP120 package="TO220 [THT]"]
  D1 = Diode [part_number=1N4001 package=diode-1n4001]
  R2 = Resistor [tolerance=±5% resistance=220 package=THT]
  R3 = Resistor [tolerance=±5% resistance=1k package=THT]
  R1 = Resistor [tolerance=±5% resistance=10k package=THT]
  Wasser_Sensor = female pin header, 2 pins [form="♀ (female)"]
  Magnet_Ventil = female pin header, 2 pins [form="♀ (female)"]
  FTDI = FTDI_BASIC [package=ftdi_basic]
  12VDC = female pin header, 2 pins [form="♀ (female)"]

nets:
  N1: IC1.GND, C1.-, U1.Pin_4, LED1.cathode, Q1.emitter, D1.A, Wasser_Sensor.pin2, FTDI.5, 12VDC.pin1
  N2: IC1.IN, Magnet_Ventil.pin2, 12VDC.pin2
  N3: IC1.OUT, C1.+, U1.Pin_8, R1.Pin_0
  N4: U1.Pin_1, R1.Pin_1
  N5: U1.Pin_2, FTDI.3
  N6: U1.Pin_3, FTDI.2
  N7: U1.Pin_5, R2.Pin_0
  N8: U1.Pin_7, Wasser_Sensor.pin1
  N9: LED1.anode, R2.Pin_1, R3.Pin_0
  N10: Q1.base, R3.Pin_1
  N11: Q1.collector, D1.C, Magnet_Ventil.pin1

notes:
  Wasser-Sensor
  Magnet-Ventil
  FTDI
  12VDC
